# Fritzing sketch suedwind_ambientika_solo_esphome (saved by Fritzing 1.0.4)
breadboards: 1

parts:
  WeMos_D1_Mini1 = WeMos D1 Mini
  MP1584EN = buck regulator mp1584en
  5V_Relay = 1 chan 5v relay module
  GP8403 = DFR0971
  Power_plug1 = Power plug
  F1 = Fan - 4 wire [package=THT]
  Placeholder = DC Motor [voltage_(max)=6V voltage_(min)=3V]
  Power_plug2 = Power plug

nets:
  N1: WeMos_D1_Mini1.5V, MP1584EN.Pin_5, MP1584EN.Pin_6, 5V_Relay.pin_1, GP8403.Pin_7
  N2: WeMos_D1_Mini1.D1, GP8403.Pin_5
  N3: WeMos_D1_Mini1.D2, GP8403.Pin_4
  N4: WeMos_D1_Mini1.D4, 5V_Relay.pin_3
  N5: WeMos_D1_Mini1.G, MP1584EN.Pin_7, MP1584EN.Pin_8, 5V_Relay.pin_2, GP8403.Pin_6
  GND: MP1584EN.Pin_1, MP1584EN.Pin_2, Power_plug1.GND, F1.GND
  N6: MP1584EN.Pin_4, Power_plug1.VCC, F1.Power
  N7: 5V_Relay.pin_4, Placeholder.pin_2
  N8: 5V_Relay.pin_5, Power_plug2.GND
  N9: GP8403.Pin_3, F1.PWM
  N10: Placeholder.pin_1, Power_plug2.VCC

notes:
  24V DC
  5V DC
  Südwind Ambientika Solo+ Fan Control
  Program ESP-Home to send desired voltages to fan:
  Forward | Reverse
  High: 7.28 V | 3.12 V
  Mid: 6.48 V | 3.58 V
  Low: 5.85 V | 4.33 V
  The relais controls the 230V deliverd to the "100331.14" actuator, which keeps the ventilation flap open during operation
  AZDelivery
  ESP32 D1 Mini

custom parts:
  WeMos D1 Mini: The D1 mini is a mini wifi board based on ESP-8266EX.
  buck regulator mp1584en: Mini MP1584EN DC to DC buck converter module with a wide operating range.
  1 chan 5v relay module: 1 Channel 5V Relay Module Board Shield with Optocoupler Support High and Low Level Trigger for Arduino.
  DFR0971: 2-Channel I2C DAC Module (0-10V).
  Fan - 4 wire: Fan, 4 wire with tach.
